// Logisim project cpu.circ as structural Verilog: 9 circuits, main circuit main
module base_5_encoder (
  input  _0,
  input  _1,
  input  _2,
  input  _3,
  input  _4,
  input  _5,
  input  _6,
  input  _7,
  input  _8,
  input  _9,
  input  _10,
  input  _11,
  input  _12,
  input  _13,
  input  _14,
  input  _15,
  output five_a,
  output five_b,
  output five_c,
  output five_d,
  output five_e,
  output five_f,
  output five_g,
  output one_a,
  output one_b,
  output one_c,
  output one_d,
  output one_e,
  output one_f,
  output one_g
);

  wire or_1_out, or_2_out, or_3_out, or_4_out, or_5_out, or_6_out, or_7_out, or_8_out, or_9_out, or_10_out,
       or_11_out, or_12_out, or_13_out, or_14_out, or_15_out, or_16_out, or_17_out, or_18_out, or_19_out,
       or_21_out, or_22_out, or_23_out, or_24_out, or_25_out, or_27_out, or_28_out, or_31_out, or_34_out;

  or or_1 (or_1_out, _0, _10);
  or or_2 (or_2_out, _1, _11);
  or or_3 (or_3_out, _2, _12);
  or or_4 (or_4_out, _3, _13);
  or or_5 (or_5_out, _4, _14);
  or or_6 (or_6_out, or_1_out, _15);
  or or_7 (or_7_out, or_6_out, _5);
  or or_8 (or_8_out, or_2_out, _6);
  or or_9 (or_9_out, or_3_out, _7);
  or or_10 (or_10_out, or_4_out, _8);
  or or_11 (or_11_out, or_5_out, _9);
  or or_12 (or_12_out, _3, _4);
  or or_13 (or_13_out, _8, _9);
  or or_14 (or_14_out, _13, _14);
  or or_15 (or_15_out, or_4_out, or_5_out);
  or or_16 (or_16_out, _2, or_12_out);
  or or_17 (or_17_out, _7, or_13_out);
  or or_18 (or_18_out, _12, or_14_out);
  or or_19 (or_19_out, or_3_out, or_15_out);
  or or_20 (one_e, or_9_out, or_7_out);
  or or_21 (or_21_out, or_10_out, or_11_out);
  or or_22 (or_22_out, _1, or_16_out);
  or or_23 (or_23_out, _6, or_17_out);
  or or_24 (or_24_out, _11, or_18_out);
  or or_25 (or_25_out, or_2_out, or_19_out);
  or or_26 (five_f, _0, or_22_out);
  or or_27 (or_27_out, _5, or_23_out);
  or or_28 (or_28_out, _10, or_24_out);
  or or_29 (five_e, or_1_out, or_25_out);
  or or_30 (one_a, or_10_out, one_e);
  or or_31 (or_31_out, or_21_out, or_7_out);
  or or_32 (one_f, or_11_out, or_7_out);
  or or_33 (one_g, or_21_out, or_9_out);
  or or_34 (or_34_out, _15, or_27_out);
  or or_35 (five_g, _15, or_28_out);
  or or_36 (one_c, or_8_out, or_31_out);
  or or_37 (five_a, five_e, _15);
  or or_38 (five_c, or_34_out, five_f);
  or or_39 (five_b, one_e, one_c);

  assign five_d = five_a;
  assign one_b = five_b;
  assign one_d = one_a;

  // Notes on the sheet:
  //   Fives digit
  //   Ones digit
endmodule

module main (
);

  wire base_2_decoder_1_five_a, base_2_decoder_1_five_b, base_2_decoder_1_five_c, base_2_decoder_1_five_d,
       base_2_decoder_1_five_e, base_2_decoder_1_five_f, base_2_decoder_1_five_g, base_2_decoder_1_one_a,
       base_2_decoder_1_one_b, base_2_decoder_1_one_c, base_2_decoder_1_one_d, base_2_decoder_1_one_e,
       base_2_decoder_1_one_f, base_2_decoder_1_one_g, base_2_encoder_1_b0, base_2_encoder_1_b1,
       base_2_encoder_1_b2, base_2_encoder_1_b3, base_2_encoder_2_b0, base_2_encoder_2_b1,
       base_2_encoder_2_b2, base_2_encoder_2_b3, base_5_encoder_1_five_a, base_5_encoder_1_five_b,
       base_5_encoder_1_five_c, base_5_encoder_1_five_d, base_5_encoder_1_five_e, base_5_encoder_1_five_f,
       base_5_encoder_1_five_g, base_5_encoder_1_one_a, base_5_encoder_1_one_b, base_5_encoder_1_one_c,
       base_5_encoder_1_one_d, base_5_encoder_1_one_e, base_5_encoder_1_one_f, base_5_encoder_1_one_g,
       base_5_encoder_2_five_a, base_5_encoder_2_five_b, base_5_encoder_2_five_c, base_5_encoder_2_five_d,
       base_5_encoder_2_five_e, base_5_encoder_2_five_f, base_5_encoder_2_five_g, base_5_encoder_2_one_a,
       base_5_encoder_2_one_b, base_5_encoder_2_one_c, base_5_encoder_2_one_d, base_5_encoder_2_one_e,
       base_5_encoder_2_one_f, base_5_encoder_2_one_g, calculator_1_overflow, calculator_1_s0,
       calculator_1_s1, calculator_1_s2, calculator_1_sum3, dipswitch_1_sw1, dipswitch_1_sw2,
       dipswitch_1_sw3, dipswitch_1_sw4, dipswitch_1_sw5, dipswitch_1_sw6, dipswitch_1_sw7, dipswitch_1_sw8,
       dipswitch_1_sw9, dipswitch_1_sw10, dipswitch_1_sw11, dipswitch_1_sw12, dipswitch_1_sw13,
       dipswitch_1_sw14, dipswitch_1_sw15, dipswitch_1_sw16, dipswitch_2_sw1, dipswitch_3_sw1,
       dipswitch_3_sw2, dipswitch_3_sw3, dipswitch_3_sw4, dipswitch_3_sw5, dipswitch_3_sw6, dipswitch_3_sw7,
       dipswitch_3_sw8, dipswitch_3_sw9, dipswitch_3_sw10, dipswitch_3_sw11, dipswitch_3_sw12,
       dipswitch_3_sw13, dipswitch_3_sw14, dipswitch_3_sw15, dipswitch_3_sw16;
  wire [4:0] operator_1_col0, operator_1_col1, operator_1_col2, operator_1_col3, operator_1_col4;

  base_5_encoder base_5_encoder_1 (
    .one_a(base_5_encoder_1_one_a), .one_b(base_5_encoder_1_one_b), .one_c(base_5_encoder_1_one_c),
    .one_d(base_5_encoder_1_one_d), .one_e(base_5_encoder_1_one_e), .one_f(base_5_encoder_1_one_f),
    .one_g(base_5_encoder_1_one_g), .five_a(base_5_encoder_1_five_a), .five_b(base_5_encoder_1_five_b),
    .five_c(base_5_encoder_1_five_c), .five_d(base_5_encoder_1_five_d), .five_e(base_5_encoder_1_five_e),
    .five_f(base_5_encoder_1_five_f), .five_g(base_5_encoder_1_five_g), ._1(dipswitch_1_sw2),
    ._2(dipswitch_1_sw3), ._3(dipswitch_1_sw4), ._4(dipswitch_1_sw5), ._5(dipswitch_1_sw6),
    ._6(dipswitch_1_sw7), ._7(dipswitch_1_sw8), ._8(dipswitch_1_sw9), ._9(dipswitch_1_sw10),
    ._10(dipswitch_1_sw11), ._11(dipswitch_1_sw12), ._12(dipswitch_1_sw13), ._13(dipswitch_1_sw14),
    ._14(dipswitch_1_sw15), ._15(dipswitch_1_sw16), ._0(dipswitch_1_sw1));
  DipSwitch #(.number(16)) dipswitch_1 (
    .sw1(dipswitch_1_sw1), .sw2(dipswitch_1_sw2), .sw3(dipswitch_1_sw3), .sw4(dipswitch_1_sw4),
    .sw5(dipswitch_1_sw5), .sw6(dipswitch_1_sw6), .sw7(dipswitch_1_sw7), .sw8(dipswitch_1_sw8),
    .sw9(dipswitch_1_sw9), .sw10(dipswitch_1_sw10), .sw11(dipswitch_1_sw11), .sw12(dipswitch_1_sw12),
    .sw13(dipswitch_1_sw13), .sw14(dipswitch_1_sw14), .sw15(dipswitch_1_sw15), .sw16(dipswitch_1_sw16));
  DipSwitch #(.number(2)) dipswitch_2 (.sw1(dipswitch_2_sw1));  // open: sw2
  _7_Segment_Display u_7_segment_display_1 (
    .g(base_5_encoder_1_five_g), .f(base_5_encoder_1_five_f), .a(base_5_encoder_1_five_a),
    .b(base_5_encoder_1_five_b), .e(base_5_encoder_1_five_e), .d(base_5_encoder_1_five_d),
    .c(base_5_encoder_1_five_c));  // open: dp
  _7_Segment_Display u_7_segment_display_2 (
    .g(base_5_encoder_1_one_g), .f(base_5_encoder_1_one_f), .a(base_5_encoder_1_one_a),
    .b(base_5_encoder_1_one_b), .e(base_5_encoder_1_one_e), .d(base_5_encoder_1_one_d),
    .c(base_5_encoder_1_one_c));  // open: dp
  DotMatrix #(.matrixrows(5)) dotmatrix_1 (
    .col0(operator_1_col0), .col1(operator_1_col1), .col2(operator_1_col2), .col3(operator_1_col3),
    .col4(operator_1_col4));
  operator operator_1 (
    .col0(operator_1_col0), .col1(operator_1_col1), .col2(operator_1_col2), .col3(operator_1_col3),
    .col4(operator_1_col4), .Subtract(dipswitch_2_sw1));
  base_2_encoder base_2_encoder_1 (
    .B0(base_2_encoder_1_b0), .B1(base_2_encoder_1_b1), .B2(base_2_encoder_1_b2), .B3(base_2_encoder_1_b3),
    ._0(dipswitch_1_sw1), ._1(dipswitch_1_sw2), ._2(dipswitch_1_sw3), ._3(dipswitch_1_sw4),
    ._4(dipswitch_1_sw5), ._5(dipswitch_1_sw6), ._6(dipswitch_1_sw7), ._7(dipswitch_1_sw8),
    ._8(dipswitch_1_sw9), ._9(dipswitch_1_sw10), ._10(dipswitch_1_sw11), ._11(dipswitch_1_sw12),
    ._12(dipswitch_1_sw13), ._13(dipswitch_1_sw14), ._14(dipswitch_1_sw15), ._15(dipswitch_1_sw16));
  _7_Segment_Display u_7_segment_display_3 (
    .g(base_5_encoder_2_five_g), .f(base_5_encoder_2_five_f), .a(base_5_encoder_2_five_a),
    .b(base_5_encoder_2_five_b), .e(base_5_encoder_2_five_e), .d(base_5_encoder_2_five_d),
    .c(base_5_encoder_2_five_c));  // open: dp
  base_5_encoder base_5_encoder_2 (
    .one_a(base_5_encoder_2_one_a), .one_b(base_5_encoder_2_one_b), .one_c(base_5_encoder_2_one_c),
    .one_d(base_5_encoder_2_one_d), .one_e(base_5_encoder_2_one_e), .one_f(base_5_encoder_2_one_f),
    .one_g(base_5_encoder_2_one_g), .five_a(base_5_encoder_2_five_a), .five_b(base_5_encoder_2_five_b),
    .five_c(base_5_encoder_2_five_c), .five_d(base_5_encoder_2_five_d), .five_e(base_5_encoder_2_five_e),
    .five_f(base_5_encoder_2_five_f), .five_g(base_5_encoder_2_five_g), ._1(dipswitch_3_sw2),
    ._2(dipswitch_3_sw3), ._3(dipswitch_3_sw4), ._4(dipswitch_3_sw5), ._5(dipswitch_3_sw6),
    ._6(dipswitch_3_sw7), ._7(dipswitch_3_sw8), ._8(dipswitch_3_sw9), ._9(dipswitch_3_sw10),
    ._10(dipswitch_3_sw11), ._11(dipswitch_3_sw12), ._12(dipswitch_3_sw13), ._13(dipswitch_3_sw14),
    ._14(dipswitch_3_sw15), ._15(dipswitch_3_sw16), ._0(dipswitch_3_sw1));
  DipSwitch #(.number(16)) dipswitch_3 (
    .sw1(dipswitch_3_sw1), .sw2(dipswitch_3_sw2), .sw3(dipswitch_3_sw3), .sw4(dipswitch_3_sw4),
    .sw5(dipswitch_3_sw5), .sw6(dipswitch_3_sw6), .sw7(dipswitch_3_sw7), .sw8(dipswitch_3_sw8),
    .sw9(dipswitch_3_sw9), .sw10(dipswitch_3_sw10), .sw11(dipswitch_3_sw11), .sw12(dipswitch_3_sw12),
    .sw13(dipswitch_3_sw13), .sw14(dipswitch_3_sw14), .sw15(dipswitch_3_sw15), .sw16(dipswitch_3_sw16));
  _7_Segment_Display u_7_segment_display_4 (
    .g(base_5_encoder_2_one_g), .f(base_5_encoder_2_one_f), .a(base_5_encoder_2_one_a),
    .b(base_5_encoder_2_one_b), .e(base_5_encoder_2_one_e), .d(base_5_encoder_2_one_d),
    .c(base_5_encoder_2_one_c));  // open: dp
  DotMatrix #(.matrixrows(5)) dotmatrix_2 (
    .col0(5'b01010), .col1(5'b01010), .col2(5'b01010), .col3(5'b01010), .col4(5'b01010));
  base_2_encoder base_2_encoder_2 (
    .B0(base_2_encoder_2_b0), .B1(base_2_encoder_2_b1), .B2(base_2_encoder_2_b2), .B3(base_2_encoder_2_b3),
    ._0(dipswitch_3_sw1), ._1(dipswitch_3_sw2), ._2(dipswitch_3_sw3), ._3(dipswitch_3_sw4),
    ._4(dipswitch_3_sw5), ._5(dipswitch_3_sw6), ._6(dipswitch_3_sw7), ._7(dipswitch_3_sw8),
    ._8(dipswitch_3_sw9), ._9(dipswitch_3_sw10), ._10(dipswitch_3_sw11), ._11(dipswitch_3_sw12),
    ._12(dipswitch_3_sw13), ._13(dipswitch_3_sw14), ._14(dipswitch_3_sw15), ._15(dipswitch_3_sw16));
  calculator calculator_1 (
    .Overflow(calculator_1_overflow), .Sum3(calculator_1_sum3), .S2(calculator_1_s2), .S1(calculator_1_s1),
    .S0(calculator_1_s0), .A3(base_2_encoder_1_b3), .B3(base_2_encoder_2_b3), .A2(base_2_encoder_1_b2),
    .B2(base_2_encoder_2_b2), .A1(base_2_encoder_1_b1), .B1(base_2_encoder_2_b1), .A0(base_2_encoder_1_b0),
    .B0(base_2_encoder_2_b0), .Subtract(dipswitch_2_sw1));
  base_2_decoder base_2_decoder_1 (
    .one_d(base_2_decoder_1_one_d), .one_e(base_2_decoder_1_one_e), .one_f(base_2_decoder_1_one_f),
    .one_g(base_2_decoder_1_one_g), .five_a(base_2_decoder_1_five_a), .five_b(base_2_decoder_1_five_b),
    .five_c(base_2_decoder_1_five_c), .five_d(base_2_decoder_1_five_d), .five_e(base_2_decoder_1_five_e),
    .five_f(base_2_decoder_1_five_f), .five_g(base_2_decoder_1_five_g), .one_a(base_2_decoder_1_one_a),
    .one_b(base_2_decoder_1_one_b), .one_c(base_2_decoder_1_one_c), .B3(calculator_1_sum3),
    .B2(calculator_1_s2), .B1(calculator_1_s1), .B0(calculator_1_s0), .Overflow(calculator_1_overflow));
  _7_Segment_Display u_7_segment_display_5 (
    .g(base_2_decoder_1_five_g), .f(base_2_decoder_1_five_f), .a(base_2_decoder_1_five_a),
    .b(base_2_decoder_1_five_b), .e(base_2_decoder_1_five_e), .d(base_2_decoder_1_five_d),
    .c(base_2_decoder_1_five_c));  // open: dp
  _7_Segment_Display u_7_segment_display_6 (
    .g(base_2_decoder_1_one_g), .f(base_2_decoder_1_one_f), .a(base_2_decoder_1_one_a),
    .b(base_2_decoder_1_one_b), .e(base_2_decoder_1_one_e), .d(base_2_decoder_1_one_d),
    .c(base_2_decoder_1_one_c));  // open: dp

  // Notes on the sheet:
  //   Subtraction
  //   0 1 2 3 4 5 6 7 8 9 0 1 2 3 4 5
  //   Signed
  //   1 1 1 1 1 1
  //   1 1 1 1 1 1
  //   0 1 2 3 4 5 6 7 8 9 0 1 2 3 4 5
endmodule

module base_2_encoder (
  input  _0,
  input  _1,
  input  _2,
  input  _3,
  input  _4,
  input  _5,
  input  _6,
  input  _7,
  input  _8,
  input  _9,
  input  _10,
  input  _11,
  input  _12,
  input  _13,
  input  _14,
  input  _15,
  output B0,
  output B1,
  output B2,
  output B3
);

  wire or_1_out, or_2_out, or_3_out, or_4_out, or_5_out, or_6_out, or_7_out, or_8_out, or_9_out, or_10_out,
       or_11_out, or_12_out, or_13_out, or_14_out, or_15_out, or_16_out, or_17_out, or_18_out;

  or or_1 (or_1_out, _13, _15);
  or or_2 (or_2_out, _2, _3);
  or or_3 (or_3_out, _4, _5);
  or or_4 (or_4_out, _6, _7);
  or or_5 (or_5_out, _8, _9);
  or or_6 (or_6_out, _10, _11);
  or or_7 (or_7_out, _12, _13);
  or or_8 (or_8_out, _14, _15);
  or or_9 (or_9_out, _11, or_1_out);
  or or_10 (or_10_out, _9, or_9_out);
  or or_11 (or_11_out, or_2_out, or_4_out);
  or or_12 (or_12_out, or_3_out, or_4_out);
  or or_13 (or_13_out, _5, or_14_out);
  or or_14 (or_14_out, _7, or_10_out);
  or or_15 (or_15_out, or_6_out, or_8_out);
  or or_16 (or_16_out, or_5_out, or_6_out);
  or or_17 (or_17_out, or_7_out, or_8_out);
  or or_18 (or_18_out, _3, or_13_out);
  or or_19 (B0, _1, or_18_out);
  or or_20 (B1, or_11_out, or_15_out);
  or or_21 (B2, or_12_out, or_17_out);
  or or_22 (B3, or_16_out, or_17_out);
endmodule

module half_adder (
  input  A,
  input  B,
  output Sum,
  output Carry
);

  xor xor_1 (Sum, B, A);
  and and_1 (Carry, B, A);
endmodule

module full_adder (
  input  A,
  input  B,
  input  Carry_in,
  output Carry_out,
  output Sum
);

  wire half_adder_1_carry, half_adder_1_sum, half_adder_2_carry;

  half_adder half_adder_1 (.Sum(half_adder_1_sum), .Carry(half_adder_1_carry), .A(A), .B(B));
  half_adder half_adder_2 (.Sum(Sum), .Carry(half_adder_2_carry), .A(half_adder_1_sum), .B(Carry_in));
  or or_1 (Carry_out, half_adder_1_carry, half_adder_2_carry);
endmodule

module mux (
  input  Selector,
  input  B,
  input  A,
  output Y
);

  wire and_1_out, and_2_out, not_1_out;

  not not_1 (not_1_out, Selector);
  and and_1 (and_1_out, not_1_out, B);
  and and_2 (and_2_out, Selector, A);
  or or_1 (Y, and_1_out, and_2_out);
endmodule

module calculator (
  input  A3,
  input  A2,
  input  A1,
  input  A0,
  input  B3,
  input  B2,
  input  B1,
  input  B0,
  input  Subtract,
  output Overflow,
  output Sum3,
  output S2,
  output S1,
  output S0
);

  wire full_adder_1_carry_out, full_adder_2_carry_out, full_adder_3_carry_out, full_adder_4_carry_out,
       mux_1_y, mux_2_y, mux_3_y, mux_4_y, not_1_out, not_2_out, not_3_out, not_4_out;

  xor xor_1 (Overflow, Subtract, full_adder_1_carry_out);
  not not_1 (not_1_out, B3);
  mux mux_1 (.Y(mux_1_y), .B(B3), .A(not_1_out), .Selector(Subtract));
  full_adder full_adder_1 (
    .Carry_out(full_adder_1_carry_out), .Sum(Sum3), .A(A3), .B(mux_1_y), .Carry_in(full_adder_2_carry_out));
  full_adder full_adder_2 (
    .Carry_out(full_adder_2_carry_out), .Sum(S2), .A(A2), .B(mux_2_y), .Carry_in(full_adder_3_carry_out));
  not not_2 (not_2_out, B2);
  mux mux_2 (.Y(mux_2_y), .B(B2), .A(not_2_out), .Selector(Subtract));
  not not_3 (not_3_out, B1);
  mux mux_3 (.Y(mux_3_y), .B(B1), .A(not_3_out), .Selector(Subtract));
  full_adder full_adder_3 (
    .Carry_out(full_adder_3_carry_out), .Sum(S1), .A(A1), .B(mux_3_y), .Carry_in(full_adder_4_carry_out));
  mux mux_4 (.Y(mux_4_y), .B(B0), .A(not_4_out), .Selector(Subtract));
  full_adder full_adder_4 (.Carry_out(full_adder_4_carry_out), .Sum(S0), .A(A0), .B(mux_4_y), .Carry_in(Subtract));
  not not_4 (not_4_out, B0);
endmodule

module operator (
  input  Subtract,
  output [4:0] col0,
  output [4:0] col1,
  output [4:0] col2,
  output [4:0] col3,
  output [4:0] col4
);

  wire [4:0] bit_extender_1_out, not_1_out;

  assign bit_extender_1_out = {{4{Subtract}}, Subtract};  // Bit_Extender bit_extender_1
  assign not_1_out = ~bit_extender_1_out;  // NOT_Gate not_1, 5 bits wide
  assign col2 = 5'b00100 | not_1_out;  // OR_Gate or_1, 5 bits wide

  assign col0 = 5'b00100;
  assign col1 = 5'b00100;
  assign col3 = 5'b00100;
  assign col4 = 5'b00100;
endmodule

module base_2_decoder (
  input  Overflow,
  input  B3,
  input  B2,
  input  B1,
  input  B0,
  output five_a,
  output five_b,
  output five_c,
  output five_d,
  output five_e,
  output five_f,
  output five_g,
  output one_a,
  output one_b,
  output one_c,
  output one_d,
  output one_e,
  output one_f,
  output one_g
);

  wire and_1_out, and_2_out, and_3_out, and_4_out, and_5_out, and_6_out, and_7_out, and_8_out, and_9_out,
       and_10_out, and_11_out, and_12_out, and_13_out, and_14_out, and_15_out, and_16_out, and_17_out,
       and_18_out, and_19_out, and_20_out, and_21_out, and_22_out, and_23_out, and_24_out, and_25_out,
       and_26_out, and_27_out, nor_1_out, nor_2_out, nor_3_out, nor_4_out, nor_5_out, not_1_out, not_2_out,
       not_3_out, not_4_out, not_5_out, or_1_out, or_2_out, or_3_out, or_4_out, or_5_out, or_6_out, or_7_out,
       or_8_out, or_9_out, or_10_out, or_11_out, or_12_out, or_13_out, or_14_out, or_15_out, or_16_out,
       or_17_out, or_18_out, or_19_out, or_20_out, or_21_out, or_22_out, or_23_out, or_24_out, or_25_out,
       or_26_out, or_27_out, or_28_out;

  not not_1 (not_1_out, B3);
  not not_2 (not_2_out, B2);
  not not_3 (not_3_out, B1);
  not not_4 (not_4_out, B0);
  and and_1 (and_1_out, B3, B2);
  and and_2 (and_2_out, B3, B1);
  and and_3 (and_3_out, B3, B0);
  and and_4 (and_4_out, B2, B1);
  and and_5 (and_5_out, B2, B0);
  and and_6 (and_6_out, B1, B0);
  nor nor_1 (nor_1_out, B3, B2);
  nor nor_2 (nor_2_out, B3, B1);
  nor nor_3 (nor_3_out, B2, B1);
  nor nor_4 (nor_4_out, B2, B0);
  nor nor_5 (nor_5_out, B1, B0);
  or or_1 (or_1_out, and_1_out, and_2_out);
  and and_7 (and_7_out, and_6_out, B2);
  and and_8 (and_8_out, and_1_out, not_3_out);
  and and_9 (and_9_out, nor_5_out, not_1_out);
  and and_10 (and_10_out, not_2_out, B1);
  and and_11 (and_11_out, and_2_out, not_4_out);
  or or_2 (or_2_out, and_5_out, nor_4_out);
  and and_12 (and_12_out, not_1_out, and_6_out);
  or or_3 (or_3_out, and_2_out, nor_2_out);
  and and_13 (and_13_out, B0, not_2_out);
  and and_14 (and_14_out, B3, not_2_out);
  and and_15 (and_15_out, not_4_out, and_4_out);
  or or_4 (or_4_out, not_1_out, B1);
  or or_5 (or_5_out, and_5_out, nor_4_out);
  and and_16 (and_16_out, and_1_out, nor_5_out);
  and and_17 (and_17_out, not_1_out, nor_5_out);
  and and_18 (and_18_out, B2, nor_2_out);
  and and_19 (and_19_out, B1, and_1_out);
  and and_20 (and_20_out, not_4_out, and_2_out);
  and and_21 (and_21_out, and_3_out, nor_3_out);
  and and_22 (and_22_out, not_3_out, B3);
  and and_23 (and_23_out, nor_1_out, B1);
  and and_24 (and_24_out, nor_5_out, B2);
  and and_25 (and_25_out, B2, nor_5_out);
  or or_6 (or_6_out, nor_1_out, or_1_out);
  or or_7 (or_7_out, and_7_out, nor_3_out);
  or or_8 (or_8_out, nor_1_out, and_9_out);
  or or_9 (or_9_out, and_10_out, and_11_out);
  or or_10 (or_10_out, and_8_out, and_12_out);
  or or_11 (or_11_out, and_3_out, or_3_out);
  or or_12 (or_12_out, and_14_out, and_15_out);
  and and_26 (and_26_out, or_4_out, or_5_out);
  or or_13 (or_13_out, and_20_out, and_21_out);
  or or_14 (or_14_out, and_23_out, and_24_out);
  or or_15 (or_15_out, and_25_out, or_6_out);
  or or_16 (or_16_out, or_7_out, not_1_out);
  or or_17 (or_17_out, or_8_out, or_9_out);
  or or_18 (or_18_out, and_13_out, or_12_out);
  and and_27 (and_27_out, and_15_out, B3);
  or or_19 (or_19_out, and_22_out, or_14_out);
  or or_20 (or_20_out, and_8_out, or_17_out);
  or or_21 (or_21_out, or_2_out, or_10_out);
  or or_22 (or_22_out, and_26_out, and_16_out);
  or or_23 (or_23_out, and_19_out, or_13_out);
  or or_24 (or_24_out, and_12_out, and_27_out);
  or or_25 (or_25_out, or_11_out, or_18_out);
  or or_26 (or_26_out, and_18_out, or_23_out);
  or or_27 (or_27_out, or_24_out, or_19_out);
  not not_5 (not_5_out, Overflow);
  or or_28 (or_28_out, and_17_out, or_26_out);
  or or_29 (five_a, Overflow, or_15_out);
  and and_28 (five_b, not_5_out, 1'b1);
  and and_29 (five_c, not_5_out, or_16_out);
  or or_30 (five_d, or_15_out, Overflow);
  or or_31 (five_e, Overflow, or_20_out);
  or or_32 (five_f, Overflow, or_8_out);
  or or_33 (five_g, or_1_out, Overflow);
  and and_30 (one_a, or_21_out, not_5_out);
  and and_31 (one_b, not_5_out, 1'b1);
  and and_32 (one_c, or_25_out, not_5_out);
  or or_34 (one_e, Overflow, or_22_out);
  and and_33 (one_f, not_5_out, or_28_out);
  or or_35 (one_g, Overflow, or_27_out);

  assign one_d = one_a;

  // Notes on the sheet:
  //   32
  //   31
  //   21
  //   20
  //   10
  //   32
  //   31
  //   21
  //   20
  //   10
endmodule
